# Fritzing sketch Circuit (saved by Fritzing 0.9.5d)
breadboards: 1

parts:
  MCU1 = Raspberry Pi Zero  # not connected
  MCU2 = Raspberry Pi Zero
  U1 = MPU 9250 Breakout [package="SIP (Single Inline) [THT]"]
  S1 = Pushbutton [package="[SMD]"]

nets:
  N1: MCU2.pin_1, MCU2.pin_2, MCU2.pin_3, MCU2.pin_4, MCU2.pin_17, MCU2.pin_18, U1.VCC, U1.SDA, S1.Pin_3, S1.Pin_4
  N2: MCU2.pin_5, MCU2.pin_6, MCU2.pin_9, MCU2.pin_10, MCU2.pin_13, MCU2.pin_14, MCU2.pin_19, MCU2.pin_20, MCU2.pin_25, MCU2.pin_26, MCU2.pin_29, MCU2.pin_30, MCU2.pin_33, MCU2.pin_34, MCU2.pin_39, MCU2.pin_40, U1.GND, U1.SCL, S1.Pin_1, S1.Pin_2
  N3: MCU2.pin_7, MCU2.pin_8
  N4: MCU2.pin_11, MCU2.pin_12
  N5: MCU2.pin_15, MCU2.pin_16
  N6: MCU2.pin_21, MCU2.pin_22
  N7: MCU2.pin_23, MCU2.pin_24
  N8: MCU2.pin_27, MCU2.pin_28
  N9: MCU2.pin_31, MCU2.pin_32
  N10: MCU2.pin_35, MCU2.pin_36
  N11: MCU2.pin_37, MCU2.pin_38

custom parts:
  MPU 9250 Breakout: Generic MPU 9250 Breakout Board
